# Fritzing sketch sketch-v0-0-1 (saved by Fritzing 0.9.4)
breadboards: 1

parts:
  Part1 = Arduino Uno (Rev3)
  U1 = ESP8266 WiFi Module [part_number=ESP8266]
  U3 = Voltage Regulator - 3.3V [package="TO220 [THT]"]

nets:
  N1: Part1.D10_PWM/SS, U1.IO0
  N2: Part1.D11_PWM/MOSI, U1.IO14
  N3: Part1.5V, U3.output_voltage
  N4: Part1.GND, U1.IO15, U3.input_voltage
  N5: U1.IO2, U1.CLK, U3.GND

notes:
  Voltage Regulatoir
  LV1117AV33
  Converts 5v from Arduino to
  stable 3.3v as required by
  ESP8266 ESP-01
  5v - red
  3.3v - orange
  ESP8266 ESP-01 WiFi
  TXD -> D10 (RX)
  CHP0 -> 3.3v
  RST -> nil
  VCC -> 3.3v
  GND -> GND
  GP2 -> nil
  GP0 -> nil
  RX0 -> D11 (TX)
